# Fritzing sketch Carbon Monoxide - LCD Nokia5110 (saved by Fritzing 0.8.7b)
circuit board: 8.46667cm x 5.64444cm
breadboards: 2

parts:
  Componente1 = Arduino Uno (Rev3)
  Nokia_5110_LCD_Module1 = Nokia5110LCDModule
  R1 = Resistor [tolerance=±5% resistance=10k package=THT]
  U1 = MQ7 - Carbon Monoxide [package=mq-3]

nets:
  N1: Componente1.A0, U1.AOUT
  N2: Componente1.D3_PWM, Nokia_5110_LCD_Module1.SCLK
  N3: Componente1.D4, Nokia_5110_LCD_Module1.6_DN_(MOSI)
  N4: Componente1.D5_PWM, Nokia_5110_LCD_Module1.D/C
  N5: Componente1.D6_PWM, Nokia_5110_LCD_Module1.RST
  N6: Componente1.D7, Nokia_5110_LCD_Module1.SCE
  3V3: Componente1.3V3, Nokia_5110_LCD_Module1.Vcc
  5V: Componente1.5V, R1.Pin_1, U1.VCC
  GND: Componente1.GND, U1.GND
  N7: Nokia_5110_LCD_Module1.LED, R1.Pin_0

custom parts:
  : Nokia 5110 LCD with 8 pin. It's a 45mm*45mm module part. Description: The Nokia 5110 is a basic graphic LCD screen for lots of applications. It was originally intended for as a cell phone screen. This one is mounted on an easy to solder PCB. It uses the PCD8544 controller. The PCD8544 is a low power CMOS LCD controller/driver, designed to drive a graphic display of 48 rows and 84 columns. All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
