# Fritzing sketch Temperatura e Umidade (saved by Fritzing 0.8.7b)
breadboards: 1

parts:
  Componente1 = Arduino Uno (Rev3)
  RHT1 = Humidity and Temperature Sensor RHT03

nets:
  N1: Componente1.A1, RHT1.GND_1
  5V: Componente1.5V, RHT1.Vcc
  N2: Componente1.GND, RHT1.GND_2
