# Fritzing sketch Atualização FirmWare (saved by Fritzing 0.8.7b)
breadboards: 1

parts:
  U1 = ESP8266 WiFi Module [part_number=ESP8266]
  FTDI_USB = FTDI Basic Programmer
  Fonte_3_3V = Breadboard Power Supply Board SMD

nets:
  N1: U1.RXD, FTDI_USB.TXO
  VCC: U1.VCC, U1.CH_PD, Fonte_3_3V.VCC
  GND: U1.GPIO_0, U1.GND, Fonte_3_3V.GND
  N2: U1.TXD, FTDI_USB.RXI

notes:
  Fonte ajustada em 3.3V
  Atualização de Firmware:GPIO0 ligado apenas enquanto faz upload

custom parts:
  ESP8266 WiFi Module: Generic WiFi Module based on the ESP8266 with onboard PCB antenna and UART communications
