# Fritzing sketch Conexão Simples (saved by Fritzing 0.8.7b)
breadboards: 1

parts:
  U1 = ESP8266 WiFi Module [part_number=ESP8266]
  Arduíno = Arduino Uno (Rev3)

nets:
  N1: U1.RXD, Arduíno.D0/RX
  VCC: U1.VCC, U1.CH_PD, Arduíno.3V3
  GND: U1.GND, Arduíno.GND
  N2: U1.TXD, Arduíno.D1/TX

notes:
  Não Recomendado.
  Ideal utilizar Regulador de Tensão.

custom parts:
  ESP8266 WiFi Module: Generic WiFi Module based on the ESP8266 with onboard PCB antenna and UART communications
