# Fritzing sketch Exemplo Led (saved by Fritzing 0.8.7b)
breadboards: 1

parts:
  U1 = ESP8266 WiFi Module [part_number=ESP8266]
  Fonte_3_3V = Breadboard Power Supply Board SMD
  FTDI_USB = FTDI Basic Programmer
  LED1 = LED - 5mm [color="Green (570nm)" package="5 mm [THT]"]
  LED2 = LED - 5mm [color="Red (633nm)" package="5 mm [THT]"]
  R1 = Resistor [tolerance=±5% resistance=110 package=THT]
  R2 = Resistor [tolerance=±5% resistance=110 package=THT]

nets:
  N1: U1.RXD, FTDI_USB.TXO
  VCC: U1.VCC, U1.CH_PD, Fonte_3_3V.VCC
  N2: U1.GPIO_0, R2.Pin_1
  N3: U1.GPIO_2, R1.Pin_1
  GND: U1.GND, Fonte_3_3V.GND, LED1.cathode, LED2.cathode
  N4: U1.TXD, FTDI_USB.RXI
  N5: LED1.anode, R2.Pin_0
  N6: LED2.anode, R1.Pin_0

notes:
  Fonte ajustada em 3.3V

custom parts:
  ESP8266 WiFi Module: Generic WiFi Module based on the ESP8266 with onboard PCB antenna and UART communications
