# Fritzing sketch Soil Moisture Humidity (saved by Fritzing 0.8.7b)

parts:
  Componente1 = Arduino Uno (Rev3)
  J1 = female pin header, 4 pins [form="♀ (female)"]

nets:
  N1: Componente1.A0, J1.pin1
  N2: Componente1.5V, J1.pin4
  N3: Componente1.GND, J1.pin3

notes:
  A0 D0 GND VCC
