# Fritzing sketch Stepper Motor - Joystick (saved by Fritzing 0.8.7b)
breadboards: 1

parts:
  Componente1 = Arduino Uno (Rev3)
  X1 = X113647 Stepper Driver Board [package=board]
  MOTOR1 = 28BYJ-48 Stepper Motor
  Componente2 = Thumb Joystick

nets:
  N1: Componente1.A0, Componente2.HORZ
  N2: Componente1.A1, Componente2.VERT
  N3: Componente1.D8, X1.IN1
  N4: Componente1.D9_PWM, X1.IN2
  N5: Componente1.D10_PWM/SS, X1.IN3
  N6: Componente1.D11_PWM/MOSI, X1.IN4
  GND: Componente1.GND, X1.GND, Componente2.GND
  N7: Componente1.D2, Componente2.SEL
  5V: Componente1.5V, X1.+V, Componente2.VCC
  N8: X1.BLUE, MOTOR1.BLUE
  N9: X1.PINK, MOTOR1.PINK
  N10: X1.YELLOW, MOTOR1.RED
  N11: X1.ORANGE, MOTOR1.ORANGE
  N12: X1.RED, MOTOR1.YELLOW

custom parts:
  X113647 Stepper Driver Board: A common stepper motor driver board based on ULN2003APG darlington array
  28BYJ-48 Stepper Motor: 28BYJ-48 gear-reduction stepper motor (small)
